# Fritzing sketch AnalogSensorsPotAndDistance (saved by Fritzing 0.7.10b)
breadboards: 1

parts:
  LED2 = LED - 5mm [color="Red (633nm)" package="5 mm [THT]"]
  R1 = Rotary Potentiometer (Large) [maximum_resistance=100kΩ package=THT]
  Arduino2 = Arduino
  J1 = Infrared Proximity Sensor

nets:
  GND: LED2.cathode, R1.leg2, Arduino2.GND, J1.GND
  N1: LED2.anode, Arduino2.D13
  +5V: R1.leg1, Arduino2.+5V, J1.Vcc
  N2: R1.wiper, Arduino2.A3
  N3: Arduino2.A0, J1.Vout

notes:
  In this example, potentiometer values are read in through an 'Analog In' pin. The values are then used to control the blinking rate of an LED. Related example: http://arduino.cc/en/Tutorial/AnalogInput
