# Fritzing sketch AnalogSensorsWithLEDsAndPushButton (saved by Fritzing 0.7.12b)
breadboards: 1

parts:
  R4 = Resistor [resistance=220 tolerance=±5% package=THT]
  R3 = Resistor [resistance=220 tolerance=±5% package=THT]
  R1 = Resistor [resistance=220 tolerance=±5% package=THT]
  R2 = Resistor [resistance=220 tolerance=±5% package=THT]
  R5 = Resistor [resistance=220 tolerance=±5% package=THT]
  R6 = Resistor [resistance=220 tolerance=±5% package=THT]
  LED3 = LED - 5mm [color="Green (555nm)" package="5 mm [THT]"]
  LED6 = LED - 5mm [color="Red (633nm)" package="5 mm [THT]"]
  LED2 = LED - 5mm [color="Yellow (585nm)" package="5 mm [THT]"]
  LED5 = LED - 5mm [color="Red (633nm)" package="5 mm [THT]"]
  LED4 = LED - 5mm [color="Green (555nm)" package="5 mm [THT]"]
  Arduino = Arduino
  S1 = Pushbutton [package=THT]
  R7 = Resistor [tolerance=±5% resistance=220 package=THT]
  LED1 = LED - 5mm [color="Yellow (585nm)" package="5 mm [THT]"]
  R8 = Rotary Potentiometer (Small) [maximum_resistance=100kΩ]
  J1 = Basic Force Sensing Resistor (FSR) [package=THT]
  R9 = Photocell (LDR) [package=THT]  # not connected
  J2 = Infrared Proximity Sensor
  T1 = LM35 Temperature Sensor [package="TO92 [THT]"]
  R10 = Resistor [tolerance=±5% resistance=10k package=THT]
  R11 = Resistor [tolerance=±5% resistance=10k package=THT]  # not connected

nets (from the breadboard view):
  N1: R4.Pin_0, LED4.anode
  N2: R4.Pin_1, Arduino.D9
  N3: R3.Pin_0, LED3.anode
  N4: R3.Pin_1, Arduino.D6
  N5: R1.Pin_0, LED1.anode
  N6: R1.Pin_1, Arduino.D3
  N7: R2.Pin_0, LED2.anode
  N8: R2.Pin_1, Arduino.D5
  N9: R5.Pin_0, LED5.anode
  N10: R5.Pin_1, Arduino.D10
  N11: R6.Pin_0, LED6.anode
  N12: R6.Pin_1, Arduino.D11
  GND: LED3.cathode, LED6.cathode, LED2.cathode, LED5.cathode, LED4.cathode, Arduino.GND, S1.leg0, LED1.cathode, T1.GND, R10.Pin_0
  N13: Arduino.+5V, Arduino.A1, J1.pin_1, T1.+Vs
  N14: Arduino.A0, T1.Vout
  N15: Arduino.A2, R10.Pin_1
  N16: Arduino.A3, J2.Vout
  N17: Arduino.A4, R8.wiper
  N18: S1.leg1, R7.Pin_1
  N19: R8.leg1, J2.GND

notes:
  File name: PhysComLEDsAndPushButton

// code stored in the sketch: Loop.ino
/*
  For Loop Iteration
 
 Demonstrates the use of a for() loop. 
 Lights multiple LEDs in sequence, then in reverse.
 
 The circuit:
 * LEDs from pins 2 through 7 to ground
 
 created 2006
 by David A. Mellis
 modified 30 Aug 2011
 by Tom Igoe 

This example code is in the public domain.
 
 http://www.arduino.cc/en/Tutorial/ForLoop
 */

int timer = 100;           // The higher the number, the slower the timing.

void setup() {
  // use a for loop to initialize each pin as an output:
  for (int thisPin = 2; thisPin < 8; thisPin++)  {
    pinMode(thisPin, OUTPUT);      
  }
}

void loop() {
  // loop from the lowest pin to the highest:
  for (int thisPin = 2; thisPin < 8; thisPin++) { 
    // turn the pin on:
    digitalWrite(thisPin, HIGH);   
    delay(timer);                  
    // turn the pin off:
    digitalWrite(thisPin, LOW);    
  }

  // loop from the highest pin to the lowest:
  for (int thisPin = 7; thisPin >= 2; thisPin--) { 
    // turn the pin on:
    digitalWrite(thisPin, HIGH);
    delay(timer);
    // turn the pin off:
    digitalWrite(thisPin, LOW);
  }
}
