# Fritzing sketch CountingRotaryEncoderAdvanced-4bit (saved by Fritzing 0.7.12b)
breadboards: 1

parts:
  Arduino1 = Arduino
  S1 = Pushbutton [package=THT]
  S2 = Pushbutton [package=THT]
  R1 = Resistor [tolerance=±5% resistance=220 package=THT]
  R2 = Resistor [tolerance=±5% resistance=220 package=THT]
  RE1 = Rotary Encoder [package=THT]
  LED1 = LED - 5mm [color="Red (633nm)" package="5 mm [THT]"]
  LED2 = LED - 5mm [color="Red (633nm)" package="5 mm [THT]"]
  R3 = Resistor [tolerance=±5% resistance=220 package=THT]
  R4 = Resistor [tolerance=±5% resistance=220 package=THT]
  R5 = Resistor [tolerance=±5% resistance=220 package=THT]
  R6 = Resistor [tolerance=±5% resistance=220 package=THT]
  R7 = Resistor [tolerance=±5% resistance=220 package=THT]
  R8 = Resistor [tolerance=±5% resistance=220 package=THT]
  7_Segment1 = 7 Segment Display
  R10 = Resistor [tolerance=±5% resistance=1k package=THT]
  R11 = Resistor [tolerance=±5% resistance=1k package=THT]
  LED4 = LED - 5mm [color="Red (633nm)" package="5 mm [THT]"]
  LED5 = LED - 5mm [color="Red (633nm)" package="5 mm [THT]"]
  LED6 = LED - 5mm [color="Red (633nm)" package="5 mm [THT]"]
  LED7 = LED - 5mm [color="Red (633nm)" package="5 mm [THT]"]

nets:
  N1: Arduino1.D12, 7_Segment1.Segment_G
  N2: Arduino1.D11, 7_Segment1.Segment_F
  N3: Arduino1.D10, 7_Segment1.Segment_A
  N4: Arduino1.D9, 7_Segment1.Segment_B
  N5: Arduino1.D8, 7_Segment1.Segment_C
  N6: Arduino1.D7, 7_Segment1.Segment_D
  N7: Arduino1.D6, 7_Segment1.Segment_E
  N8: Arduino1.D5, Arduino1.D4, Arduino1.+5V, S1.leg0, S2.leg0, RE1.EncoderPinC
  N9: Arduino1.D3, LED1.cathode, R3.Pin_1
  N10: Arduino1.D2, LED2.cathode, R4.Pin_1
  N11: Arduino1.GND, R1.Pin_0, R2.Pin_0, R3.Pin_0, R4.Pin_0, R10.Pin_1, R11.Pin_0, LED4.cathode, LED5.cathode, LED6.cathode, LED7.cathode
  N12: Arduino1.A0, R5.Pin_0
  N13: Arduino1.A1, R6.Pin_0
  N14: Arduino1.A2, R7.Pin_0
  N15: Arduino1.A3, R8.Pin_0
  N16: S1.leg1, R2.Pin_1
  N17: S2.leg1, R1.Pin_1
  N18: RE1.EncoderPinA, LED1.anode
  N19: RE1.EncoderPinB, LED2.anode
  N20: R5.Pin_1, LED4.anode
  N21: R6.Pin_1, LED5.anode
  N22: R7.Pin_1, LED6.anode
  N23: R8.Pin_1, LED7.anode
  N24: 7_Segment1.common_anode, R10.Pin_0, R11.Pin_1

notes:
  File name: CountingRotaryEncoderAdvanced-4bit.fzz
