# Fritzing sketch CountingRotaryEncoderAdvancedRGBLEDs (saved by Fritzing 0.7.12b)
breadboards: 1

parts:
  Arduino1 = Arduino
  S1 = Pushbutton [package=THT]
  S2 = Pushbutton [package=THT]
  R1 = Resistor [tolerance=±5% resistance=220 package=THT]
  R2 = Resistor [tolerance=±5% resistance=220 package=THT]
  RE1 = Rotary Encoder [package=THT]
  LED1 = LED - 5mm [color="Red (633nm)" package="5 mm [THT]"]
  LED2 = LED - 5mm [color="Red (633nm)" package="5 mm [THT]"]
  R3 = Resistor [tolerance=±5% resistance=220 package=THT]
  R4 = Resistor [tolerance=±5% resistance=220 package=THT]
  LED3 = LED - 5mm [color="Red (633nm)" package="5 mm [THT]"]
  R5 = Resistor [tolerance=±5% resistance=220 package=THT]
  LED4 = LED - 5mm [color="Red (633nm)" package="5 mm [THT]"]
  LED5 = LED - 5mm [color="Red (633nm)" package="5 mm [THT]"]
  LED6 = LED - 5mm [color="Red (633nm)" package="5 mm [THT]"]
  R6 = Resistor [tolerance=±5% resistance=220 package=THT]
  R7 = Resistor [tolerance=±5% resistance=220 package=THT]
  R8 = Resistor [tolerance=±5% resistance=220 package=THT]
  7_Segment1 = 7 Segment Display
  R10 = Resistor [tolerance=±5% resistance=1k package=THT]
  R11 = Rotary Potentiometer (Small) [maximum_resistance=100kΩ]
  LED7 = RGB LED (com. anode, rbg) [package="5 mm [THT]"]
  LED8 = RGB LED (com. anode, rbg) [package="5 mm [THT]"]
  R12 = Resistor [tolerance=±5% resistance=220 package=THT]
  R13 = Resistor [tolerance=±5% resistance=220 package=THT]
  R14 = Resistor [tolerance=±5% resistance=220 package=THT]  # not connected
  R15 = Resistor [tolerance=±5% resistance=220 package=THT]
  R16 = Resistor [tolerance=±5% resistance=220 package=THT]
  R17 = Resistor [tolerance=±5% resistance=220 package=THT]

nets:
  N1: Arduino1.D11, R12.Pin_0
  N2: Arduino1.D10, R13.Pin_0
  N3: Arduino1.D9, R17.Pin_0
  N4: Arduino1.D5, R16.Pin_0
  N5: Arduino1.D3, R15.Pin_0
  N6: Arduino1.+5V, S1.leg0, S2.leg0, RE1.EncoderPinC, R10.Pin_0, R11.leg2, LED7.common_anode
  N7: Arduino1.GND, R1.Pin_0, R2.Pin_0, R3.Pin_0, R4.Pin_0, LED3.cathode, LED4.cathode, LED5.cathode, LED6.cathode, R11.leg1, LED8.common_anode
  N8: Arduino1.A0, R11.wiper
  N9: Arduino1.A2, LED1.cathode, R3.Pin_1
  N10: Arduino1.A3, LED2.cathode, R4.Pin_1
  N11: Arduino1.A4, S2.leg1, R1.Pin_1, 7_Segment1.Segment_A
  N12: Arduino1.A5, S1.leg1, R2.Pin_1
  N13: RE1.EncoderPinA, LED1.anode
  N14: RE1.EncoderPinB, LED2.anode
  N15: LED3.anode, R5.Pin_1
  N16: LED4.anode, R6.Pin_1
  N17: LED5.anode, R7.Pin_1
  N18: LED6.anode, R8.Pin_1
  N19: 7_Segment1.common_anode, R10.Pin_1
  N20: LED7.red_cathode, R12.Pin_1
  N21: LED7.blue_cathode, R13.Pin_1
  N22: LED7.green_cathode, R17.Pin_1
  N23: LED8.blue_cathode, R16.Pin_1
  N24: LED8.green_cathode, R15.Pin_1

notes:
  File name: CountingRotaryEncoderAdvancedRGBLEDs
