# Fritzing sketch Fade_with_Button (saved by Fritzing 0.7.11b)
breadboards: 1

parts:
  S1 = Pushbutton [package=THT]
  R1 = Resistor [resistance=10k tolerance=±5% package=THT]
  LED1 = LED - 5mm [color="Red (633nm)" package="5 mm [THT]"]
  Arduino2 = Arduino

nets (from the schematic view):
  N1: S1.leg0, Arduino2.+5V
  N2: S1.leg1, R1.Pin_1, Arduino2.D2
  N3: R1.Pin_0, LED1.cathode, Arduino2.GND
  N4: LED1.anode, Arduino2.D9
