# Fritzing sketch LED on Board (saved by Fritzing 0.7.4b)
breadboards: 1

parts:
  Arduino1 = Arduino
  LED1 = LED - 5mm [color="Red (633nm)" package="5 mm [THT]"]

nets:
  N1: Arduino1.D13, LED1.anode
  N2: Arduino1.GND, LED1.cathode
