# Fritzing sketch Parking-Assistant (saved by Fritzing 0.7.11b)
breadboards: 1

parts:
  IR_Sensor_1 = Infrared Proximity Sensor
  220Ω = Resistor [resistance=220 tolerance=±5% package=THT]
  220Ω_2 = Resistor [resistance=220 tolerance=±5% package=THT]
  220Ω_3 = Resistor [resistance=220 tolerance=±5% package=THT]
  220Ω_4 = Resistor [resistance=220 tolerance=±5% package=THT]
  220Ω_5 = Resistor [resistance=220 tolerance=±5% package=THT]
  LED2 = LED - 5mm [color="Green (555nm)" package="5 mm [THT]"]
  LED4 = LED - 5mm [color="Red (633nm)" package="5 mm [THT]"]
  LED3 = LED - 5mm [color="Red (633nm)" package="5 mm [THT]"]
  LED2_2 = LED - 5mm [color="Yellow (585nm)" package="5 mm [THT]"]
  LED2_3 = LED - 5mm [color="Yellow (585nm)" package="5 mm [THT]"]
  Parking_Assistant = Arduino

nets:
  N1: IR_Sensor_1.Vout, Parking_Assistant.A1
  GND: IR_Sensor_1.GND, LED2.cathode, LED4.cathode, LED3.cathode, LED2_2.cathode, LED2_3.cathode, Parking_Assistant.GND
  5V: IR_Sensor_1.Vcc, Parking_Assistant.+5V
  N2: 220Ω.Pin_0, LED2_2.anode
  N3: 220Ω.Pin_1, Parking_Assistant.D6
  N4: 220Ω_2.Pin_0, LED2_3.anode
  N5: 220Ω_2.Pin_1, Parking_Assistant.D5
  N6: 220Ω_3.Pin_0, LED3.anode
  N7: 220Ω_3.Pin_1, Parking_Assistant.D3
  N8: 220Ω_4.Pin_0, LED4.anode
  N9: 220Ω_4.Pin_1, Parking_Assistant.D2
  N10: 220Ω_5.Pin_0, LED2.anode
  N11: 220Ω_5.Pin_1, Parking_Assistant.D4

notes:
  Simple Parking Assistant
  The distance to objects in the proximity is measured and displayed as led graph.
