# Fritzing sketch RotaryEncoder_Basic (saved by Fritzing 0.7.12b)
breadboards: 1

parts:
  Arduino1 = Arduino
  RE1 = Rotary Encoder [package=THT]
  LED1 = LED - 5mm [color="Red (633nm)" package="5 mm [THT]"]
  LED2 = LED - 5mm [color="Red (633nm)" package="5 mm [THT]"]
  R3 = Resistor [tolerance=±5% resistance=220 package=THT]
  R4 = Resistor [tolerance=±5% resistance=220 package=THT]

nets:
  N1: Arduino1.D3, LED1.cathode, R3.Pin_1
  N2: Arduino1.D2, LED2.cathode, R4.Pin_1
  N3: Arduino1.+5V, RE1.EncoderPinC
  N4: Arduino1.GND, R3.Pin_0, R4.Pin_0
  N5: RE1.EncoderPinA, LED1.anode
  N6: RE1.EncoderPinB, LED2.anode

notes:
  File name: RotaryEncoder_Basic.fzz
